// Logisim project Somador CarryLookahead.circ as structural Verilog: 2 circuits, main circuit main
module main (
  input  A___MSB,
  input  A___LSB,
  input  B___MSB,
  input  B___LSB,
  input  Cin,
  output MSB,
  output OVERFLOW,
  output LSB
);

  wire and_1_out, and_2_out, and_3_out, and_4_out, and_5_out, or_2_out, or_3_out, or_4_out;

  or or_1 (OVERFLOW, and_3_out, and_1_out, and_2_out);
  and and_1 (and_1_out, or_2_out, and_5_out);
  and and_2 (and_2_out, or_2_out, or_4_out, Cin);
  and and_3 (and_3_out, A___MSB, B___MSB);
  or or_2 (or_2_out, A___MSB, B___MSB);
  adder adder_1 (.A(A___MSB), .B(B___MSB), .Cin(or_3_out), .out_4(MSB));
  or or_3 (or_3_out, and_5_out, and_4_out);
  and and_4 (and_4_out, or_4_out, Cin);
  and and_5 (and_5_out, A___LSB, B___LSB);
  or or_4 (or_4_out, A___LSB, B___LSB);
  adder adder_2 (.A(A___LSB), .B(B___LSB), .Cin(Cin), .out_4(LSB));

  // Notes on the sheet:
  //   Count-1
  //   Resultado da soma
  //   count-Gerador1
  //   count-Propagação1
endmodule

module adder (
  input  A,
  input  B,
  input  Cin,
  output out_4
);

  wire xor_1_out;

  xor xor_1 (xor_1_out, B, Cin);
  xor xor_2 (out_4, A, xor_1_out);

  // Notes on the sheet:
  //   Resultado da soma
endmodule
