// Logisim project carryskip-logisim-v3.circ as structural Verilog: 1 circuit, main circuit main
module main (
  input  C0__IN,
  input  A0,
  input  B0,
  input  A1,
  input  B1,
  input  A2,
  input  B2,
  input  A3,
  input  B3,
  output S0,
  output S1,
  output S2,
  output S3,
  output C3__OUT
);

  wire and_1_out, and_2_out, and_3_out, and_4_out, and_5_out, and_6_out, and_7_out, and_8_out, and_9_out,
       and_10_out, and_11_out, and_12_out, and_13_out, not_1_out, or_1_out, or_2_out, or_3_out, or_4_out,
       xor_1_out, xor_2_out, xor_3_out, xor_4_out;

  xor xor_1 (xor_1_out, A0, B0);
  xor xor_2 (xor_2_out, A1, B1);
  xor xor_3 (xor_3_out, A2, B2);
  xor xor_4 (xor_4_out, A3, B3);
  and and_1 (and_1_out, B0, A0);
  and and_2 (and_2_out, B1, A1);
  and and_3 (and_3_out, B2, A2);
  and and_4 (and_4_out, B3, A3);
  and and_5 (and_5_out, xor_2_out, xor_1_out);
  and and_6 (and_6_out, xor_3_out, or_2_out);
  and and_7 (and_7_out, xor_4_out, or_3_out);
  and and_8 (and_8_out, xor_3_out, and_5_out);
  and and_9 (and_9_out, xor_2_out, or_1_out);
  and and_10 (and_10_out, xor_4_out, and_8_out);
  and and_11 (and_11_out, xor_1_out, C0__IN);
  or or_1 (or_1_out, and_11_out, and_1_out);
  or or_2 (or_2_out, and_9_out, and_2_out);
  or or_3 (or_3_out, and_6_out, and_3_out);
  or or_4 (or_4_out, and_7_out, and_4_out);
  not not_1 (not_1_out, and_10_out);
  xor xor_5 (S0, xor_1_out, C0__IN);
  xor xor_6 (S1, xor_2_out, or_1_out);
  xor xor_7 (S2, xor_3_out, or_2_out);
  xor xor_8 (S3, xor_4_out, or_3_out);
  and and_12 (and_12_out, C0__IN, and_10_out);
  and and_13 (and_13_out, not_1_out, or_4_out);
  or or_5 (C3__OUT, and_12_out, and_13_out);
endmodule
