// Logisim project carryskip-logisim.circ as structural Verilog: 1 circuit, main circuit main
module main (
  input  A0,
  input  B0,
  input  C0__IN,
  input  A1,
  input  B1,
  input  A2,
  input  B2,
  input  A3,
  input  B3,
  output M0,
  output P0,
  output S0,
  output C__OUT,
  output MS,
  output C0__OUT,
  output M1,
  output P1,
  output S1,
  output C1__IN,
  output C1__OUT,
  output P2,
  output S2,
  output C2__IN,
  output C2__OUT,
  output P3,
  output S0_2,
  output C3__IN,
  output C3__OUT
);

  wire and_1_out, and_2_out, and_3_out, and_4_out, and_5_out, and_6_out, and_7_out, and_8_out, and_10_out,
       and_11_out, not_1_out;

  xor xor_1 (P0, A0, B0);
  and and_1 (and_1_out, A0, B0);
  xor xor_2 (P1, A1, B1);
  and and_2 (and_2_out, A1, B1);
  xor xor_3 (P2, A2, B2);
  and and_3 (and_3_out, A2, B2);
  xor xor_4 (P3, A3, B3);
  and and_4 (and_4_out, A3, B3);
  and and_5 (and_5_out, C0__IN, P0);
  and and_6 (and_6_out, C0__OUT, P1);
  and and_7 (and_7_out, C1__OUT, P2);
  and and_8 (and_8_out, C2__OUT, P3);
  xor xor_5 (S0, P0, C0__IN);
  or or_1 (C0__OUT, and_5_out, and_1_out);
  xor xor_6 (S1, P1, C0__OUT);
  or or_2 (C1__OUT, and_6_out, and_2_out);
  xor xor_7 (S2, P2, C1__OUT);
  or or_3 (C2__OUT, and_7_out, and_3_out);
  xor xor_8 (S0_2, P3, C2__OUT);
  or or_4 (C3__OUT, and_8_out, and_4_out);
  and and_9 (MS, P0, P1, P2, P3);
  not not_1 (not_1_out, MS);
  and and_10 (and_10_out, C0__IN, MS);
  and and_11 (and_11_out, not_1_out, C3__OUT);
  or or_5 (C__OUT, and_10_out, and_11_out);

  assign C1__IN = C0__OUT;
  assign C2__IN = C1__OUT;
  assign C3__IN = C2__OUT;
  assign M0 = C0__IN;
  assign M1 = C3__OUT;
endmodule
