// Logisim project full adder.circ as structural Verilog: 3 circuits, main circuit main
module main (
  input  A,
  input  B,
  input  Cin,
  input  sub_zero,
  input  B_2,
  input  B_3,
  input  in_7,
  input  B_4,
  input  B_5,
  input  B_6,
  input  B_7,
  input  B_8,
  input  A_2,
  input  A_3,
  input  A_4,
  input  A_5,
  input  A_6,
  input  A_7,
  input  A_8,
  input  A_9,
  output out_21,
  output Cout,
  output out_23,
  output out_24,
  output out_25,
  output out_26,
  output out_27,
  output out_28,
  output out_29,
  output out_30,
  output out_31
);

  wire full_adder_3_cout, full_adder_4_cout, full_adder_5_cout, full_adder_6_cout, full_adder_7_cout,
       full_adder_8_cout, full_adder_9_cout, xor_1_out, xor_2_out, xor_3_out, xor_4_out, xor_5_out,
       xor_6_out, xor_7_out, xor_8_out;

  xor xor_1 (xor_1_out, B_2, sub_zero);
  FULL_ADDER full_adder_1 (.A(A_2), .B(xor_1_out), .Cin(full_adder_3_cout), .soma(out_24), .Cout(out_23));
  FULL_ADDER full_adder_2 (.A(A), .B(B), .Cin(Cin), .soma(out_21), .Cout(Cout));
  xor xor_2 (xor_2_out, B_3, sub_zero);
  FULL_ADDER full_adder_3 (.A(A_3), .B(xor_2_out), .Cin(full_adder_4_cout), .soma(out_25), .Cout(full_adder_3_cout));
  xor xor_3 (xor_3_out, in_7, sub_zero);
  FULL_ADDER full_adder_4 (.A(A_4), .B(xor_3_out), .Cin(full_adder_5_cout), .soma(out_26), .Cout(full_adder_4_cout));
  xor xor_4 (xor_4_out, B_4, sub_zero);
  FULL_ADDER full_adder_5 (.A(A_5), .B(xor_4_out), .Cin(full_adder_6_cout), .soma(out_27), .Cout(full_adder_5_cout));
  xor xor_5 (xor_5_out, B_5, sub_zero);
  FULL_ADDER full_adder_6 (.A(A_6), .B(xor_5_out), .Cin(full_adder_7_cout), .soma(out_28), .Cout(full_adder_6_cout));
  xor xor_6 (xor_6_out, B_6, sub_zero);
  FULL_ADDER full_adder_7 (.A(A_7), .B(xor_6_out), .Cin(full_adder_8_cout), .soma(out_29), .Cout(full_adder_7_cout));
  xor xor_7 (xor_7_out, B_7, sub_zero);
  FULL_ADDER full_adder_8 (.A(A_8), .B(xor_7_out), .Cin(full_adder_9_cout), .soma(out_30), .Cout(full_adder_8_cout));
  xor xor_8 (xor_8_out, B_8, sub_zero);
  FULL_ADDER full_adder_9 (.A(A_9), .B(xor_8_out), .Cin(sub_zero), .soma(out_31), .Cout(full_adder_9_cout));

  // Notes on the sheet:
  //   Resultado da soma
  //   Circuito Somador/subtrador utilizando full adder
  //   Resultado
endmodule

module FULL_ADDER (
  input  A,
  input  B,
  input  Cin,
  output soma,
  output Cout
);

  wire and_1_out, and_2_out, and_3_out, xor_1_out;

  xor xor_1 (xor_1_out, B, Cin);
  and and_1 (and_1_out, B, Cin);
  and and_2 (and_2_out, B, A);
  and and_3 (and_3_out, Cin, A);
  xor xor_2 (soma, A, xor_1_out);
  or or_1 (Cout, and_1_out, and_2_out, and_3_out);

  // Notes on the sheet:
  //   A
  //   B
  //   Cin
  //   Resultado da soma
  //   Cout
endmodule

module Half_adder (
  input  A,
  input  B,
  output out_3,
  output Cout
);

  and and_1 (Cout, A, B);
  xor xor_1 (out_3, A, B);

  // Notes on the sheet:
  //   Resultado da soma
endmodule
