// Logisim project mux.circ as structural Verilog: 1 circuit, main circuit main
module main (
  input  in_1,
  input  in_2,
  input  in_3,
  input  in_4,
  input  in_5,
  input  in_6,
  output out_7,
  output out_8
);

  wire and_1_out, and_2_out, and_4_out, and_5_out, not_1_out;

  and and_1 (and_1_out, in_2, in_3);
  and and_2 (and_2_out, in_4, in_5);
  and and_3 (out_8, and_1_out, and_2_out);
  not not_1 (not_1_out, out_8);
  and and_4 (and_4_out, in_1, out_8);
  and and_5 (and_5_out, not_1_out, in_6);
  or or_1 (out_7, and_4_out, and_5_out);
endmodule
