// Logisim project safe.circ as structural Verilog: 3 circuits, main circuit main
module main (
  input  [7:0] D
);

  FLIPFLOP_D_MOD flipflop_d_mod_1 ();  // open: D, Clock, Q
endmodule

module FLIPFLOP_D_MOD (
  input  D,
  input  Clock,
  output Q
);

  wire nand_1_out, nand_2_out, nand_4_out, not_1_out;

  not not_1 (not_1_out, D);
  nand nand_1 (nand_1_out, D, Clock);
  nand nand_2 (nand_2_out, not_1_out, Clock);
  nand nand_3 (Q, nand_1_out, nand_4_out);
  nand nand_4 (nand_4_out, Q, nand_2_out);
endmodule

module _8bits (
  input  [7:0] entrada_8_bits,
  input  SX,
  input  SY,
  input  write,
  input  Leitura,
  input  [7:0] entrada_8_bits_2,
  output [7:0] out_7,
  output [7:0] out_8,
  output [7:0] out_9,
  output [7:0] out_10,
  output [7:0] out_11
);

  wire and_1_out, Clock_out, not_1_out;

  Clock Clock (.out(Clock_out));
  and and_1 (and_1_out, Clock_out, SX, SY, write);
  FLIPFLOP_D_MOD flipflop_d_mod_1 (.D(entrada_8_bits[0]), .Clock(and_1_out), .Q(out_7[0]));
  not not_1 (not_1_out, write);
  assign out_11 = {8{Leitura}} & entrada_8_bits_2;  // AND_Gate and_2, 8 bits wide
  FLIPFLOP_D_MOD flipflop_d_mod_2 (.D(entrada_8_bits[1]), .Clock(and_1_out), .Q(out_7[1]));
  FLIPFLOP_D_MOD flipflop_d_mod_3 (.D(entrada_8_bits[2]), .Clock(and_1_out), .Q(out_7[2]));
  assign out_9 = {{7{1'b0}}, not_1_out};  // Bit_Extender bit_extender_1
  FLIPFLOP_D_MOD flipflop_d_mod_4 (.D(entrada_8_bits[3]), .Clock(and_1_out), .Q(out_7[3]));
  FLIPFLOP_D_MOD flipflop_d_mod_5 (.D(entrada_8_bits[4]), .Clock(and_1_out), .Q(out_7[4]));
  assign out_8 = out_7 & out_9;  // AND_Gate and_3, 8 bits wide
  FLIPFLOP_D_MOD flipflop_d_mod_6 (.D(entrada_8_bits[5]), .Clock(and_1_out), .Q(out_7[5]));
  FLIPFLOP_D_MOD flipflop_d_mod_7 (.D(entrada_8_bits[6]), .Clock(and_1_out), .Q(out_7[6]));
  FLIPFLOP_D_MOD flipflop_d_mod_8 (.D(entrada_8_bits[7]), .Clock(and_1_out), .Q(out_7[7]));

  assign out_10 = {8{Leitura}};
endmodule
