// Logisim project teste de decodifcador.circ as structural Verilog: 1 circuit, main circuit main
module main (
  input  [7:0] in_1,
  input  [1:0] in_2,
  input  in_3,
  input  [1:0] in_4,
  output [1:0] out_5,
  output [7:0] out_6,
  output [7:0] out_7,
  output out_8,
  output out_9,
  output [1:0] out_10,
  output [1:0] out_11
);

  Decoder #(.enable("false")) decoder_1 (.out0(out_8), .out1(out_9), .sel(in_3));
  Decoder #(.enable("false")) decoder_2 (.out0(out_10[0]), .out1(out_11[0]), .sel(in_4[0]));
  BitSelector #(.group(2)) bitselector_1 (.in(in_1), .out(out_5), .sel(in_2));
  // Pins of 1 and 2 bits meet at out_10
  // Pins of 1 and 2 bits meet at out_11
  // Pins of 1 and 2 bits meet at in_4

  assign out_6 = in_1;
  assign out_7 = in_1;
endmodule
