// Logisim project concluido.circ as structural Verilog: 4 circuits, main circuit main
module main (
  input  [7:0] D
);

  FLIPFLOP_D_MOD flipflop_d_mod_1 ();  // open: D, Clock, Q
endmodule

module FLIPFLOP_D_MOD (
  input  D,
  input  Clock,
  output Q
);

  wire nand_1_out, nand_2_out, nand_4_out, not_1_out;

  not not_1 (not_1_out, D);
  nand nand_1 (nand_1_out, D, Clock);
  nand nand_2 (nand_2_out, not_1_out, Clock);
  nand nand_3 (Q, nand_1_out, nand_4_out);
  nand nand_4 (nand_4_out, Q, nand_2_out);
endmodule

module _8bits (
  input  [7:0] entrada_8_bits,
  input  CLock,
  input  SX,
  input  SY,
  input  write,
  output [7:0] out_6
);

  wire and_2_out;
  wire [7:0] flipflop_d_mod_1_q, not_1_out;
  wire [7:7] and_1_out;

  and and_1 (and_1_out[7], SX, SY);
  and and_2 (and_2_out, CLock, and_1_out[7], write);
  FLIPFLOP_D_MOD flipflop_d_mod_1 (.D(entrada_8_bits[0]), .Clock(and_2_out), .Q(flipflop_d_mod_1_q[0]));
  FLIPFLOP_D_MOD flipflop_d_mod_2 (.D(entrada_8_bits[1]), .Clock(and_2_out), .Q(flipflop_d_mod_1_q[1]));
  FLIPFLOP_D_MOD flipflop_d_mod_3 (.D(entrada_8_bits[2]), .Clock(and_2_out), .Q(flipflop_d_mod_1_q[2]));
  assign not_1_out = ~{8{write}};  // NOT_Gate not_1, 8 bits wide
  FLIPFLOP_D_MOD flipflop_d_mod_4 (.D(entrada_8_bits[4]), .Clock(and_2_out), .Q(flipflop_d_mod_1_q[4]));
  FLIPFLOP_D_MOD flipflop_d_mod_5 (.D(entrada_8_bits[3]), .Clock(and_2_out), .Q(flipflop_d_mod_1_q[3]));
  assign out_6 = flipflop_d_mod_1_q & {8{and_1_out[7]}} & not_1_out;  // AND_Gate and_3, 8 bits wide
  FLIPFLOP_D_MOD flipflop_d_mod_6 (.D(entrada_8_bits[5]), .Clock(and_2_out), .Q(flipflop_d_mod_1_q[5]));
  FLIPFLOP_D_MOD flipflop_d_mod_7 (.D(entrada_8_bits[6]), .Clock(and_2_out), .Q(flipflop_d_mod_1_q[6]));
  FLIPFLOP_D_MOD flipflop_d_mod_8 (.D(entrada_8_bits[7]), .Clock(and_2_out), .Q(flipflop_d_mod_1_q[7]));
endmodule

module \final  (
  input  [7:0] Entrada,
  input  \Endereço ,
  input  in_3,
  input  Write,
  input  Read,
  output [7:0] out_6,
  output [7:0] out_7,
  output [7:0] out_8,
  output [7:0] out_9
);

  wire clock_1_out, decoder_1_out0, decoder_1_out1, decoder_2_out0, decoder_2_out1;
  wire [7:0] n8bits_1_out_6, n8bits_2_out_6, n8bits_3_out_6, n8bits_4_out_6, or_2_out;

  Clock #(.lowDuration(5)) clock_1 (.out(clock_1_out));
  Decoder #(.enable("false")) decoder_1 (.out0(decoder_1_out0), .out1(decoder_1_out1), .sel(in_3));
  Decoder #(.enable("false")) decoder_2 (.out0(decoder_2_out0), .out1(decoder_2_out1), .sel(\Endereço ));
  _8bits u_8bits_1 (
    .entrada_8_bits(Entrada), .CLock(clock_1_out), .SX(decoder_1_out0), .SY(decoder_2_out0), .write(Write),
    .out_6(n8bits_1_out_6));
  _8bits u_8bits_2 (
    .entrada_8_bits(Entrada), .CLock(clock_1_out), .SX(decoder_1_out1), .SY(decoder_2_out0), .write(Write),
    .out_6(n8bits_2_out_6));
  _8bits u_8bits_3 (
    .entrada_8_bits(Entrada), .CLock(clock_1_out), .SX(decoder_1_out0), .SY(decoder_2_out1), .write(Write),
    .out_6(n8bits_3_out_6));
  _8bits u_8bits_4 (
    .entrada_8_bits(Entrada), .CLock(clock_1_out), .SX(decoder_1_out1), .SY(decoder_2_out1), .write(Write),
    .out_6(n8bits_4_out_6));
  assign out_9 = n8bits_1_out_6 | n8bits_2_out_6;  // OR_Gate or_1, 8 bits wide
  assign or_2_out = n8bits_3_out_6 | n8bits_4_out_6;  // OR_Gate or_2, 8 bits wide
  assign out_8 = or_2_out | out_9;  // OR_Gate or_3, 8 bits wide
  assign out_7 = {8{Read}} & out_8;  // AND_Gate and_1, 8 bits wide

  assign out_6 = {8{Read}};

  // Notes on the sheet:
  //   SX
  //   00
  //   10
  //   SY
  //   01
  //   11
endmodule
